// Digital circuit fpga.dig as structural Verilog
module fpga (
  input  [15:0] inst,
  input  [2:0] i,
  input  pop,
  input  we_nostos,
  input  clk,
  input  mux_itos,
  input  mux_ytos,
  input  store,
  output [15:0] ros,
  output [15:0] tos,
  output [11:0] sp,
  output [15:0] nos,
  output [15:0] o,
  output [7:0] i_2
);

  wire [2:0] PC_out;
  wire [7:0] microcode_d, program_d;
  wire [15:0] bitextender_1_out;

  Counter #(.Bits(3)) PC (.en(1'b1), .C(clk), .clr(1'b0), .out(PC_out));  // open: ovf
  EEPROMDualPort #(.AddrBits(3), .Bits(16)) \program  (
    .A(PC_out), .Din(inst), .str(store), .C(clk), .ld(1'b1), .D({i_2, program_d}));
  ROM #(.AddrBits(8), .Bits(8)) microcode (.A(program_d), .sel(1'b1), .D(microcode_d));
  LED push (.in(microcode_d[0]));
  LED u_pop (.in(microcode_d[1]));
  LED i_gt_tos (.in(microcode_d[2]));
  LED nos_gt_tos (.in(microcode_d[3]));
  LED y_gt_tos (.in(microcode_d[4]));
  BitExtender bitextender_1 (.in(i_2), .out(bitextender_1_out));
  stack stack_1 (
    .clk(clk), .push(microcode_d[0]), .pop(microcode_d[1]), .i(bitextender_1_out), .y(o),
    .we_nostos(microcode_d[2]), .we_itos(microcode_d[3]), .we_ytos(microcode_d[4]), .tos(tos), .ros(ros),
    .nos(nos), .sp(sp));
  Add #(.Bits(16)) add_1 (.a(nos), .b(tos), .c_i(1'b0), .s(o));  // open: c_o

  // Other names for the same wires on the sheet: c = clk

  // Notes on the sheet:
  //   contents of program (hex, n*v repeats v):
  //   100,201,1,402,1,702,1,2
  //   FPGA Stack Machine
  //   contents of microcode (hex, n*v repeats v):
  //   5,12,a,9
endmodule
